// Logisim project solutions.circ as structural Verilog: 4 circuits, main circuit main
module main (
);


  // Notes on the sheet:
  //   Use the pane on the left to navigate between files.
  //   EECS Decal 6 - Demos and Exercises
endmodule

module L1_Simple_Gates (
  input  Inputs,
  input  in_2,
  input  in_3,
  input  in_4,
  input  in_5,
  input  in_6,
  input  in_7
);

  wire and_1_out, not_1_out, or_1_out, xor_1_out;

  not not_1 (not_1_out, Inputs);
  and and_1 (and_1_out, in_2, in_3);
  or or_1 (or_1_out, in_4, in_5);
  xor xor_1 (xor_1_out, in_6, in_7);
  // Probe on not_1_out
  // Probe on and_1_out
  // Probe on or_1_out
  // Probe on xor_1_out

  // Notes on the sheet:
  //   Use the button that looks like a finger (top left corner)
  //   to toggle inputs. Do the outputs change as you expect?
  //   Logic gates
  //   NOT
  //   AND
  //   OR
  //   XOR
  //   Outputs
endmodule

module L2_Adder (
  input  in_1,
  input  in_2,
  output [1:0] out_3
);

  and and_1 (out_3[1], in_2, in_1);
  xor xor_1 (out_3[0], in_1, in_2);

  // Notes on the sheet:
  //   You may use anything in the "Gates" subdirectory. The splitter tool 
  //   "little endian" representation (smallest bits on right).
  //   Create a 1-bit adder using logic gates
  //   allows you to split an input into bits and combine them back. Use
endmodule

module L3_ALU (
  input  [7:0] in_1,
  input  [7:0] in_2,
  input  [1:0] select,
  output [7:0] a_op_b
);

  wire [7:0] adder_1_out, divider_1_out, multiplier_1_out, subtractor_1_out;

  Adder adder_1 (.a(in_1), .b(in_2), .out(adder_1_out));  // open: cin, cout
  Subtractor subtractor_1 (.a(in_1), .b(in_2), .out(subtractor_1_out));  // open: bin, bout
  Multiplier multiplier_1 (.a(in_1), .b(in_2), .out(multiplier_1_out));  // open: cin, cout
  Divider divider_1 (.a(in_1), .b(in_2), .out(divider_1_out));  // open: upper, rem
  Multiplexer #(.select(2), .width(8), .enable("false")) multiplexer_1 (
    .in0(adder_1_out), .in1(subtractor_1_out), .in2(multiplier_1_out), .in3(divider_1_out), .out(a_op_b),
    .sel(select));

  // Other names for the same wires on the sheet: a[7:0] = in_1; b[7:0] = in_2

  // Notes on the sheet:
  //   using a multiplexer.
  //   Arithmetic logic unit (ALU)
  //   Let's say we wanted some functional unit that could do a set
  //   of arithmetic operations, not just an add. We can create this 
endmodule
